# Fritzing sketch 3d print monitor (saved by Fritzing 0.9.3b)
breadboards: 1

parts:
  Часть1 = Arduino Leonardo (Rev3b)
  Raspberry_Pi_1 = Raspberry Pi 3 [part_number=RPI-3-V1.2]  # not connected
  S1 = Momentary Switch [package=ksa_sealed_tac_switch]
  S2 = Momentary Switch [package=ksa_sealed_tac_switch]
  S3 = Momentary Switch [package=ksa_sealed_tac_switch]
  S4 = Momentary Switch [package=ksa_sealed_tac_switch]
  U1 = LCD-16X2 [package=lcd-16x2_noholes]
  J1 = Piezo Speaker

nets:
  N1: Часть1.D2/SDA, U1.DB7
  N2: Часть1.D3_PWM/SCL, U1.DB6
  N3: Часть1.D4/A6, U1.DB5
  N4: Часть1.D5_PWM, U1.DB4
  N5: Часть1.D7, S3.4
  N6: Часть1.5V, J1.pin2
  N7: Часть1.GND, J1.pin1
  N8: Часть1.D8/A8, S4.4
  N9: Часть1.D10_PWM/A10, S2.4
  N10: Часть1.D11_PWM, U1.E
  N11: Часть1.D12/A11, U1.RS
  N12: Часть1.D13_PWM, S1.4
  N13: S1.2, S2.2, S3.2, S4.2

notes:
  3d printer
  + -
  Power
  Led strip
  DIN GND VCC
  DHT21 sensor
  Sig Vcc Gnd
